# Fritzing sketch schematic (saved by Fritzing 0.9.9b)
circuit board: 8.46667cm x 5.64444cm
breadboards: 1

parts:
  Raspberry_Pi_1 = Raspberry Pi 3 [part_number=RPI-3-V1.2]
  U1 = TRANSCHIPTC5747 [package=camera_sfv24r-2st_2]  # not connected
  S1 = Pushbutton [package="[THT]"]
  LED1 = LED - 5mm [color="Red (633nm)" current=0.030 package="5 mm [THT]"]
  R1 = Resistor [tolerance=±5% power=0.25 resistance=220 package=THT]
  J1 = Infrared Proximity Sensor
  J2 = Piezo Speaker

nets:
  3V3: Raspberry_Pi_1.3v3, J1.Vcc
  N1: Raspberry_Pi_1.GPIO2, S1.Pin_1, S1.Pin_2
  N2: Raspberry_Pi_1.GPIO3, J1.Vout
  N3: Raspberry_Pi_1.GPIO4, LED1.anode
  N4: Raspberry_Pi_1.GPIO17, J2.pin2
  GND: Raspberry_Pi_1.GND, S1.Pin_3, S1.Pin_4, R1.Pin_1, J1.GND, J2.pin1
  N5: LED1.cathode, R1.Pin_0
